# Fritzing sketch google-plant (saved by Fritzing 0.9.5d)
breadboards: 1

parts:
  R1 = Photocell (LDR) [package=THT]
  Capacitive_Soil_Moisture_Sensor1 = DFRobot Capacitive Soil Moisture Sensor V1.0 [part_number=SEN0193]
  Part1 = KY-016 RGB Full Color LED Module [package="Breakout board"]
  R2 = Resistor [tolerance=±5% resistance=10k package=THT]
  J1 = female pin header, 1 pin [form="♀ (female)"]  # not connected
  J2 = female pin header, 1 pin [form="♀ (female)"]  # not connected
  J3 = female pin header, 1 pin [form="♀ (female)"]  # not connected
  J6 = female pin header, 1 pin [form="♀ (female)"]  # not connected
  U1 = ESP32-38PinWide [part_number=ESP32-38PinWide]

nets:
  N1: R1.pin_0, U1.3.3
  N2: R1.pin_1, R2.Pin_1, U1.GPIO36
  N3: Capacitive_Soil_Moisture_Sensor1.A, U1.GPIO39
  VCC: Capacitive_Soil_Moisture_Sensor1.VCC, U1.VIN
  GND: Capacitive_Soil_Moisture_Sensor1.GND, Part1.-, R2.Pin_0, U1.GPIO33, U1.GND
  N4: Part1.R, U1.GPIO12
  N5: Part1.G, U1.GPIO14
  N6: Part1.B, U1.GPIO27

custom parts:
  DFRobot Capacitive Soil Moisture Sensor V1.0: DFRobot Capacitive Soil Moisture Sensor V1.0 This product measures soil moisture levels by capacitive sensing, rather than resistive sensing like other types of moisture sensor. It is made of a corrosion resistant material giving it a long service life. Insert it into soil and impress your friends with the real-time soil moisture data! The product includes an on-board voltage regulator which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
  KY-016 RGB Full Color LED Module: KY-016 Arduino full color 5mm RGB LED, different colors can be obtained by mixing the three primary colors.
  ESP32-38PinWide: Generic 38-Pin ESP32 with wide format (only access to one side of pins on a breadboard) based on Stephen Lilley's HiLetgo ESP-WROOM-32 ESP32 ESP-32S Development Board.
